# Fritzing sketch dbox_sketch (saved by Fritzing 0.9.10b)
breadboards: 1

parts:
  DFPlayer_Mini1 = DFPlayer MINI [package="DIP (Dual Inline) [THT]"]
  R1 = Resistor [tolerance=±5% resistance=1k power=0.25 package=THT]
  R2 = Resistor [tolerance=±5% resistance=1k power=0.25 package=THT]
  J1 = Piezo Speaker
  A1 = Arduino Nano 33 BLE Sense
  J2 = Basic Force Sensing Resistor (FSR) [package=THT]
  R3 = Resistor [tolerance=±5% resistance=100k power=0.25 package=THT]
  U1 = WS2812 RGB LED strip

nets:
  VCC: DFPlayer_Mini1.VCC, A1.Pin_15, J2.pin_1, U1.VCC
  N1: DFPlayer_Mini1.RX, R2.Pin_0
  N2: DFPlayer_Mini1.TX, R1.Pin_0
  N3: DFPlayer_Mini1.SPK1, J1.pin2
  N4: DFPlayer_Mini1.GND#6, A1.Pin_14, A1.Pin_19, R3.Pin_1, U1.GND
  N5: DFPlayer_Mini1.SPK2, J1.pin1
  N6: R1.Pin_1, A1.Pin_17
  N7: R2.Pin_1, A1.Pin_16
  N8: A1.Pin_4, J2.pin_0, R3.Pin_0
  N9: A1.Pin_13, A1.Pin_18
  N10: A1.Pin_24, U1.DIN

custom parts:
  DFPlayer MINI: MP3 module by DFRobot.com for playing Music from an SD-Card. Supports WAV and MP3 files.
  Arduino Nano 33 BLE Sense: The Nano 33 BLE Sense (without headers) is Arduino’s 3.3V AI enabled board in the smallest available form factor: 45x18mm! The Arduino Nano 33 BLE Sense is a completely new board on a well-known form factor. It comes with a series of embedded sensors: 9 axis inertial sensor: what makes this board ideal for wearable devices humidity, and temperature sensor: to get highly accurate measurements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
  WS2812 RGB LED strip: WS2812 strip
